// Logisim project e21cseu016lab1micro.circ as structural Verilog: 1 circuit, main circuit main
module main (
  input  in_1,
  input  in_2,
  input  in_3,
  input  in_4,
  input  in_5,
  input  in_6,
  output out_7
);

  wire and_1_out, and_2_out, and_3_out, nand_1_out, not_1_out, not_2_out;

  not not_1 (not_1_out, in_5);
  not not_2 (not_2_out, in_6);
  and and_1 (and_1_out, in_1, not_1_out, not_2_out);
  nand nand_1 (nand_1_out, in_2, not_2_out, in_5);
  and and_2 (and_2_out, in_3, in_3, in_6, not_1_out);
  and and_3 (and_3_out, in_4, in_6, in_5);
  or or_1 (out_7, and_1_out, nand_1_out, and_2_out, and_3_out);
endmodule
