// Logisim project ques2lab1micro.circ as structural Verilog
module _2nd_ques (
  input  x,
  input  y,
  input  z,
  output c,
  output s
);

  wire and_1_out, and_2_out, and_3_out, and_4_out, and_5_out, and_6_out, and_7_out, not_1_out, not_2_out,
       not_3_out, not_4_out, not_5_out, not_6_out;

  not not_1 (not_1_out, x);
  not not_2 (not_2_out, y);
  not not_3 (not_3_out, x);
  not not_4 (not_4_out, z);
  not not_5 (not_5_out, y);
  not not_6 (not_6_out, z);
  and and_1 (and_1_out, y, z);
  and and_2 (and_2_out, x, z);
  and and_3 (and_3_out, x, y);
  and and_4 (and_4_out, not_1_out, not_2_out, z);
  and and_5 (and_5_out, not_3_out, y, not_4_out);
  and and_6 (and_6_out, x, not_5_out, not_6_out);
  and and_7 (and_7_out, x, y, z);
  or or_1 (s, and_1_out, and_2_out, and_3_out);
  or or_2 (c, and_4_out, and_5_out, and_6_out, and_7_out);
endmodule
